# Fritzing sketch cnc-wiring-1 (saved by Fritzing 1.0.5)
circuit board: 6.88566cm x 5.36311cm
breadboards: 1

parts:
  Arduino1 = Arduino Uno (Rev3)
  Power_plug2 = Power plug
  Pololu_A1 = Pololu A4988 [package=SO16]
  M2 = Stepper Motor - Bipolar
  S1 = D2F-FL Omron Snap Action Limit Switch with Level
  Mod1 = Raspberry Pi 4B  # not connected
  USBTTL1 = USB A Plug
  USBTTL2 = Micro USB B Plug

nets:
  N1: Arduino1.D8, Pololu_A1.ENABLE
  N2: Arduino1.D9_PWM, S1.Pin_2
  GND: Arduino1.GND, Power_plug2.GND, Pololu_A1.GND, S1.Pin_1
  N3: Arduino1.D2, Pololu_A1.STEP
  N4: Arduino1.D5_PWM, Pololu_A1.DIR
  5V: Arduino1.5V, Pololu_A1.VDD
  N5: Power_plug2.VCC, Pololu_A1.VMOT
  N6: Pololu_A1.RESET, Pololu_A1.SLEEP
  N7: Pololu_A1.1B, M2.D
  N8: Pololu_A1.1A, M2.B
  N9: Pololu_A1.2A, M2.C
  N10: Pololu_A1.2B, M2.A
  N11: USBTTL1.usb, USBTTL2.usb

notes:
  12 - 24 V
  The Raspberry Pi uses a serial connection over USB to communicate with the Arduino
  Limit switch

custom parts:
  D2F-FL Omron Snap Action Limit Switch with Level: Snap action switch with stainless steel lever.
